# Fritzing sketch fritzing sketch (saved by Fritzing 0.9.3b)
breadboards: 1

parts:
  Part1 = Arduino Uno (Rev3) - ICSP
  DFPlayer_Mini1 = DFPlayer MINI [package="DIP (Dual Inline) [THT]"]
  ZS-042_RTC1 = ZS-042 RTC Module
  Power_plug1 = Power plug
  S3 = Momentary Switch [package=ksa_sealed_tac_switch]
  S4 = Momentary Switch [package=ksa_sealed_tac_switch]
  S5 = Momentary Switch [package=ksa_sealed_tac_switch]
  S6 = Momentary Switch [package=ksa_sealed_tac_switch]
  S7 = Momentary Switch [package=ksa_sealed_tac_switch]
  LED2 = LED - 3mm [color="Green (555nm)" package="3 mm [THT]"]
  LED3 = LED - 3mm [color="Blue (470nm)" package="3 mm [THT]"]
  R4 = Resistor [tolerance=±5% resistance=1k package=THT]
  R5 = Resistor [tolerance=±5% resistance=1k package=THT]
  R6 = Resistor [tolerance=±5% resistance=1k package=THT]
  R7 = Resistor [tolerance=±5% resistance=1k package=THT]
  R8 = Resistor [tolerance=±5% resistance=1k package=THT]
  R1 = Resistor [tolerance=±5% resistance=220 package=THT]
  R2 = Resistor [tolerance=±5% resistance=220 package=THT]
  R3 = Resistor [tolerance=±5% resistance=220 package=THT]
  SP1 = SPEAKER [package=pcb_mount_speaker]
  R9 = Resistor [tolerance=±5% resistance=1k package=THT]
  LED1 = LED - 3mm [color="Red (633nm)" package="3 mm [THT]"]
  NEOPIXEL45 = Neopixel Strip -- Black (30/m)
  NEOPIXEL46 = Neopixel Strip -- Black (30/m)
  NEOPIXEL47 = Neopixel Strip -- Black (30/m)
  NEOPIXEL48 = Neopixel Strip -- Black (30/m)
  NEOPIXEL49 = Neopixel Strip -- Black (30/m)
  NEOPIXEL50 = Neopixel Strip -- Black (30/m)
  NEOPIXEL51 = Neopixel Strip -- Black (30/m)
  NEOPIXEL52 = Neopixel Strip -- Black (30/m)
  NEOPIXEL53 = Neopixel Strip -- Black (30/m)
  NEOPIXEL54 = Neopixel Strip -- Black (30/m)
  NEOPIXEL55 = Neopixel Strip -- Black (30/m)
  NEOPIXEL56 = Neopixel Strip -- Black (30/m)
  NEOPIXEL57 = Neopixel Strip -- Black (30/m)
  NEOPIXEL58 = Neopixel Strip -- Black (30/m)
  NEOPIXEL59 = Neopixel Strip -- Black (30/m)
  NEOPIXEL60 = Neopixel Strip -- Black (30/m)
  NEOPIXEL61 = Neopixel Strip -- Black (30/m)
  NEOPIXEL62 = Neopixel Strip -- Black (30/m)
  NEOPIXEL63 = Neopixel Strip -- Black (30/m)
  NEOPIXEL64 = Neopixel Strip -- Black (30/m)
  NEOPIXEL65 = Neopixel Strip -- Black (30/m)
  NEOPIXEL66 = Neopixel Strip -- Black (30/m)
  NEOPIXEL67 = Neopixel Strip -- Black (30/m)
  NEOPIXEL68 = Neopixel Strip -- Black (30/m)
  NEOPIXEL69 = Neopixel Strip -- Black (30/m)
  NEOPIXEL70 = Neopixel Strip -- Black (30/m)
  NEOPIXEL71 = Neopixel Strip -- Black (30/m)
  NEOPIXEL72 = Neopixel Strip -- Black (30/m)
  NEOPIXEL73 = Neopixel Strip -- Black (30/m)

nets:
  N1: Part1.A4/SDA, ZS-042_RTC1.SDA
  N2: Part1.A5/SCL, ZS-042_RTC1.SCL
  N3: Part1.D8, S3.3, R4.Pin_0
  N4: Part1.D9_PWM, S4.3, R5.Pin_0
  N5: Part1.D10_PWM/SS, S5.3, R6.Pin_0
  N6: Part1.D11_PWM/MOSI, S6.3, R7.Pin_0
  N7: Part1.D12/MISO, S7.3, R8.Pin_0
  N8: Part1.D2, DFPlayer_Mini1.TX
  N9: Part1.D3_PWM, R9.Pin_0
  N10: Part1.D4, R1.Pin_0
  N11: Part1.D5_PWM, R2.Pin_1
  N12: Part1.D6_PWM, R3.Pin_1
  N13: Part1.D7, NEOPIXEL45.DI
  VCC: DFPlayer_Mini1.VCC, Power_plug1.VCC, S3.1, S4.1, S5.1, S6.1, S7.1, NEOPIXEL45.+5V#1
  N14: DFPlayer_Mini1.SPK1, SP1.-
  GND: DFPlayer_Mini1.GND, Power_plug1.GND, LED2.anode, LED3.anode, R4.Pin_1, R5.Pin_1, R6.Pin_1, R7.Pin_1, R8.Pin_1, LED1.anode, NEOPIXEL45.GND#3
  N15: DFPlayer_Mini1.SPK2, SP1.+
  N16: LED2.cathode, R2.Pin_0
  N17: LED3.cathode, R3.Pin_0
  N18: R1.Pin_1, LED1.cathode
  N19: NEOPIXEL45.GND#4, NEOPIXEL46.GND#3
  N20: NEOPIXEL45.DO, NEOPIXEL46.DI
  N21: NEOPIXEL45.+5V#6, NEOPIXEL46.+5V#1
  N22: NEOPIXEL46.GND#4, NEOPIXEL47.GND#3
  N23: NEOPIXEL46.DO, NEOPIXEL47.DI
  N24: NEOPIXEL46.+5V#6, NEOPIXEL47.+5V#1
  N25: NEOPIXEL47.GND#4, NEOPIXEL48.GND#3
  N26: NEOPIXEL47.DO, NEOPIXEL48.DI
  N27: NEOPIXEL47.+5V#6, NEOPIXEL48.+5V#1
  N28: NEOPIXEL48.GND#4, NEOPIXEL50.GND#3
  N29: NEOPIXEL48.DO, NEOPIXEL50.DI
  N30: NEOPIXEL48.+5V#6, NEOPIXEL50.+5V#1
  N31: NEOPIXEL49.+5V#1, NEOPIXEL51.+5V#6
  N32: NEOPIXEL49.DI, NEOPIXEL51.DO
  N33: NEOPIXEL49.GND#3, NEOPIXEL51.GND#4
  N34: NEOPIXEL49.GND#4, NEOPIXEL56.GND#3
  N35: NEOPIXEL49.DO, NEOPIXEL56.DI
  N36: NEOPIXEL49.+5V#6, NEOPIXEL56.+5V#1
  N37: NEOPIXEL50.GND#4, NEOPIXEL51.GND#3
  N38: NEOPIXEL50.DO, NEOPIXEL51.DI
  N39: NEOPIXEL50.+5V#6, NEOPIXEL51.+5V#1
  N40: NEOPIXEL52.+5V#1, NEOPIXEL58.+5V#6
  N41: NEOPIXEL52.DI, NEOPIXEL58.DO
  N42: NEOPIXEL52.GND#3, NEOPIXEL58.GND#4
  N43: NEOPIXEL52.GND#4, NEOPIXEL73.GND#4
  N44: NEOPIXEL52.DO, NEOPIXEL73.DO
  N45: NEOPIXEL52.+5V#6, NEOPIXEL73.+5V#6
  N46: NEOPIXEL53.+5V#1, NEOPIXEL55.+5V#6
  N47: NEOPIXEL53.DI, NEOPIXEL55.DO
  N48: NEOPIXEL53.GND#3, NEOPIXEL55.GND#4
  N49: NEOPIXEL53.GND#4, NEOPIXEL57.GND#3
  N50: NEOPIXEL53.DO, NEOPIXEL57.DI
  N51: NEOPIXEL53.+5V#6, NEOPIXEL57.+5V#1
  N52: NEOPIXEL54.+5V#1, NEOPIXEL57.+5V#6
  N53: NEOPIXEL54.DI, NEOPIXEL57.DO
  N54: NEOPIXEL54.GND#3, NEOPIXEL57.GND#4
  N55: NEOPIXEL54.GND#4, NEOPIXEL58.GND#3
  N56: NEOPIXEL54.DO, NEOPIXEL58.DI
  N57: NEOPIXEL54.+5V#6, NEOPIXEL58.+5V#1
  N58: NEOPIXEL55.+5V#1, NEOPIXEL56.+5V#6
  N59: NEOPIXEL55.DI, NEOPIXEL56.DO
  N60: NEOPIXEL55.GND#3, NEOPIXEL56.GND#4
  N61: NEOPIXEL59.+5V#1, NEOPIXEL67.+5V#6
  N62: NEOPIXEL59.DI, NEOPIXEL67.DO
  N63: NEOPIXEL59.GND#3, NEOPIXEL67.GND#4
  N64: NEOPIXEL59.GND#4, NEOPIXEL63.GND#3
  N65: NEOPIXEL59.DO, NEOPIXEL63.DI
  N66: NEOPIXEL59.+5V#6, NEOPIXEL63.+5V#1
  N67: NEOPIXEL60.+5V#1, NEOPIXEL66.+5V#6
  N68: NEOPIXEL60.DI, NEOPIXEL66.DO
  N69: NEOPIXEL60.GND#3, NEOPIXEL66.GND#4
  N70: NEOPIXEL60.GND#4, NEOPIXEL70.GND#3
  N71: NEOPIXEL60.DO, NEOPIXEL70.DI
  N72: NEOPIXEL60.+5V#6, NEOPIXEL70.+5V#1
  N73: NEOPIXEL61.+5V#1, NEOPIXEL70.+5V#6
  N74: NEOPIXEL61.DI, NEOPIXEL70.DO
  N75: NEOPIXEL61.GND#3, NEOPIXEL70.GND#4
  N76: NEOPIXEL61.GND#4, NEOPIXEL67.GND#3
  N77: NEOPIXEL61.DO, NEOPIXEL67.DI
  N78: NEOPIXEL61.+5V#6, NEOPIXEL67.+5V#1
  N79: NEOPIXEL62.+5V#1, NEOPIXEL64.+5V#6
  N80: NEOPIXEL62.DI, NEOPIXEL64.DO
  N81: NEOPIXEL62.GND#3, NEOPIXEL64.GND#4
  N82: NEOPIXEL62.GND#4, NEOPIXEL72.GND#3
  N83: NEOPIXEL62.DO, NEOPIXEL72.DI
  N84: NEOPIXEL62.+5V#6, NEOPIXEL72.+5V#1
  N85: NEOPIXEL63.GND#4, NEOPIXEL64.GND#3
  N86: NEOPIXEL63.DO, NEOPIXEL64.DI
  N87: NEOPIXEL63.+5V#6, NEOPIXEL64.+5V#1
  N88: NEOPIXEL65.+5V#1, NEOPIXEL71.+5V#6
  N89: NEOPIXEL65.DI, NEOPIXEL71.DO
  N90: NEOPIXEL65.GND#3, NEOPIXEL71.GND#4
  N91: NEOPIXEL65.GND#4, NEOPIXEL66.GND#3
  N92: NEOPIXEL65.DO, NEOPIXEL66.DI
  N93: NEOPIXEL65.+5V#6, NEOPIXEL66.+5V#1
  N94: NEOPIXEL68.+5V, NEOPIXEL72.+5V#6
  N95: NEOPIXEL68.DI, NEOPIXEL72.DO
  N96: NEOPIXEL68.GND, NEOPIXEL72.GND#4
  N97: NEOPIXEL69.+5V#1, NEOPIXEL73.+5V#1
  N98: NEOPIXEL69.DI, NEOPIXEL73.DI
  N99: NEOPIXEL69.GND#3, NEOPIXEL73.GND#3
  N100: NEOPIXEL69.GND#4, NEOPIXEL71.GND#3
  N101: NEOPIXEL69.DO, NEOPIXEL71.DI
  N102: NEOPIXEL69.+5V#6, NEOPIXEL71.+5V#1

notes:
  WS 2811 LEDs Qty depends on your requirement

custom parts:
  DFPlayer MINI: MP3 module by DFRobot.com for playing Music from an SD-Card. Supports WAV and MP3 files.
  Neopixel Strip -- Black (30/m): Neopixel Strip, Black, 30 pixels per meter.

// code stored in the sketch: 12-11-2019_FritzingCompatiable_fullClock.ino

/*******************************************************************************************
Owner: NetworkDisa(Nuwan Dissanayake) http://networkdisa.blogspot.com
Last Modified: 20/09/2019
Phone: +94775522254

/***NOTE***
01: When set the alarm you have to set both alarm hour and minute. if you set only hour alarm wont be work.
**********/
/*******************************************************************************************/

#include <RTClib.h>
#include <Wire.h>
#include <FastLED.h>
#include "SoftwareSerial.h"
/***MP3 module default values***/
# define Start_Byte 0x7E  //Each command feedback begin with $ , that is0x7E 
# define Version_Byte 0xFF //FF --- Version Information
# define Command_Length 0x06 //the number of bytes after ?Len?, Data length is 6, which are 6 bytes [FF 06 09 00 00 04]. Not counting the start, end, and verification
# define End_Byte 0xEF //End bit 0xEF, indicate command ended
# define Acknowledge 0x00 //Returns info with command 0x41 [0x01: info, 0x00: no info] If need for feedback, 1: feedback, 0: no feedback 
SoftwareSerial mySerial(2, 3); //define SoftwareSerial RX TX pin
 
RTC_DS3231 RTC; //create RTC object
/***WS2811B related values***/
#define NUM_LEDS 86 //(3*7)*4 + 2 = 86
#define DATA_PIN 7 //data pin for pixel led(OUTPUT)
//#define COLOR_ORDER BRG  // Define color order for your strip
CRGB leds[NUM_LEDS]; // Define Pixel LEDs

void setup() {
    //Serial.begin(9600);
    Wire.begin(); // start the wire communication I2C
    RTC.begin();  // start the RTC-module
    //RTC.adjust(DateTime(2019, 10, 19, 00, 59, 0)); //YYYY,MM,DD,HH,MIN,Sec ,set RTC time first time(method-1)
    //RTC.adjust(DateTime(__DATE__, __TIME__));  //set RTC time first time,take system time(method-2)

    FastLED.addLeds<WS2812, DATA_PIN, RGB>(leds, NUM_LEDS);  //Set Pixel LED type
    LEDS.setBrightness(30);  //set initial brighness max:255
    
    mySerial.begin (9600); //begin SoftwareSerial communication with MP module
    execute_CMD(0x3F, 0, 0); // Send request for initialization parameters
    delay(500); //for mp module to work for the command sent
    execute_CMD(0x06, 0, 27); // Set the volume level(0x00~0x30)
    delay(500);
}

/*******LED Array******/
byte digits[11][21] = { //2D array for numbers on seven segments
    {0,0,0,1,1,1,1,1,1,1,1,1,1,1,1,1,1,1,1,1,1},  //Digit 0
    {0,0,0,1,1,1,0,0,0,0,0,0,0,0,0,0,0,0,1,1,1},  //Digit 1
    {1,1,1,1,1,1,1,1,1,0,0,0,1,1,1,1,1,1,0,0,0},  //Digit 2
    {1,1,1,1,1,1,1,1,1,0,0,0,0,0,0,1,1,1,1,1,1},  //Digit 3
    {1,1,1,1,1,1,0,0,0,1,1,1,0,0,0,0,0,0,1,1,1},  //Digit 4
    {1,1,1,0,0,0,1,1,1,1,1,1,0,0,0,1,1,1,1,1,1},  //Digit 5
    {1,1,1,0,0,0,1,1,1,1,1,1,1,1,1,1,1,1,1,1,1},  //Digit 6
    {0,0,0,1,1,1,1,1,1,0,0,0,0,0,0,0,0,0,1,1,1},  //Digit 7
    {1,1,1,1,1,1,1,1,1,1,1,1,1,1,1,1,1,1,1,1,1},  //Digit 8
    {1,1,1,1,1,1,1,1,1,1,1,1,0,0,0,1,1,1,1,1,1},  //Digit 9
    {0,0,0,0,0,0,1,1,1,1,1,1,1,1,1,1,1,1,0,0,0}   //Celsius character(C)
};
/*******LED Color Array******/
int colorRGB[12][3] = {
    {255,0,255},//Green
    {255,0,0},//Red
    {0,0,255},//Blue                  
    {255,255,0},//Yellow                  
    {255,0,128},//Spring Green           
    {0,255,128},//Rose                  
    {255,128,0},//Azure                    
    {128,0,255},//Chartryuse               
    {0,128,255},//Orange
    {255,0,0},//Cyan             
    {0,255,0},//Magenta                  
    {128,255,0}//Violet                  
};  
byte colorRGBIndex = 0; //ColorArray indexNo. increment every 5 seconds
byte red = 0;       //default color defined- Magenta
byte green = 255;
byte blue = 0; 

/***INPUT***/
#define btnModeInput 8  //Mode button
#define btnPlusInput 9   //+Plus+ button
#define btnMinusInput 10  //-Minus- button
#define btnSetInput 11  //Set button
#define btnAlrmOffInput 12  //Alrm Off button
/***OUTPUT***/
#define ledModDate 4  //Date edit mode indicate LED
#define ledModTime 5  //Time edit mode indicate LED       //this 3LEDs on Same time when going to Year edit mode.
#define ledModAlarm 6   //Alarm edit mode indicate LED
/***defined veriables***/
int dateTimeData[6]; //{[0]Hour, [1]Minute, [2]Seconds, [3]Month, [4]Date, [5]Year} srore real date/time values. 
int setData[] = {-1, -1, 0, 0, 0, 2017, -1, -1}; //{[0]Hour, [1]Minute, [2]Seconds, [3]Month, [4]Date, [5]Year, elarmHour[6],elarmMinute[7]} store set values. when values increment and decremt use this values.
int minMaxVal[5][2] = { //for take maxand min values.
    {0,24}, //for take 0 and <24 means 0-23 range(Hour/Min=[0][0]||Max=[0][0]) 0 is 24
    {0,60}, //for take 0 and <60 means 0-59 range(Minute/Min=[1][0]||Max=[1][1]) 0 is 60
    {1,13}, //for take 1 and <13 means 1-12 range(Month/Min=[2][0]||Max=[2][1])
    {1,32}, //for take 1 and <32 means 1-31 range(Date/Min=[3][0]||Max=[3][1])
    {2017,2050} //for year-limit year edit from 2017 to 2018. you can increment this as you wish.
};
String symbols[] = {" : "," : ","-------"," / "," /",""};  //use for serial monitor time display
unsigned long millisForClock = 0;  //this millis()value increment every 1second and store date time values in array
unsigned long millisForClockDisplay = 0; //clock values represent in LEDs every 1 seconds.
unsigned long lastPressTimeBtnMode = millis(); //update everytime after press mode button. use for disable Mode button active time(reset)
int btnModVal = -1; //starting Mode button value  
bool editMode = false; //if this mode true loop not display time and date/tempeture
bool setPosition = true; //in edit mode this value thrue means, First two digit values(Hour/Month) consider. if false (Minute/Date) values consider.
int setIndex = 0; //this val use in setValToRTC() function for direct the particular case in Switch statement.
bool alarmSet = false; //this value true when alarm set.
bool alarmBeepUntillStop = false; //become true untill press the alarm stop button.
String hexVal; //store hexadecimal value for mp module tospecify track number
byte hexaCMD[] = {0x18, 0x01, 0x02, 0x03, 0x04, 0x05, 0x06, 0x07, 0x08, 0x09, 0x0A, 0x0B, 0x0C, 0x0D, 0x0E, 0x0F, 0x10, 0x11, 0x12, 0x13, 0x14, 0x15, 0x16, 0x17}; //mp3 track number for in hexadecimal
bool alarmPlayExecute = false;  //track alarmexecutestatus

void loop() {
    //get time date values from RTC object & store dateTimeData[] array
    if(millis() - millisForClock >= 1000){ 
        millisForClock = millis();  //update time intervalcalculated value.
        DateTime now = RTC.now();  //Get the real time/date info from RTC object

        dateTimeData[0] = now.hour();   //store all the info to dateTimeData[] array. 
        dateTimeData[1] = now.minute();
        dateTimeData[2] = now.second();
        dateTimeData[3] = now.month();
        dateTimeData[4] = now.day();
        dateTimeData[5] = now.year();
        /*****only for serialmonitor display only*****
        for(byte i = 0; i < 6; i++){
            Serial.print(dateTimeData[i]); Serial.print(symbols[i]);  
        }
        Serial.print(" __AlarmData__"); Serial.print(setData[6]);Serial.print(":");Serial.print(setData[7]);
        Serial.print(" ----Edit Position="); Serial.print(btnModVal);
        Serial.println(); 
        ******************************************/
    }

    if((millis() - millisForClockDisplay >= 1000) && !editMode){//here check edit mode too. if editMode=true time not displays.
        millisForClockDisplay = millis(); 
        if(dateTimeData[2] == 35){ //color change time related 35 second.
            colorRGBIndex = (colorRGBIndex < 11) ? colorRGBIndex+1 : 0; //chk colorRGB[] array max index val exceeded or not. if exceeded reset to 0.
            red = colorRGB[colorRGBIndex][0];  //apply RGB values
            green = colorRGB[colorRGBIndex][1];
            blue = colorRGB[colorRGBIndex][2];
        }
        if(dateTimeData[2] >= 35 && dateTimeData[2] <= 40){ //every time related 35 second date display continiusely 5 seconds.
            dateGetNow(); //display date in LEDs 
            FastLED.show();   
        }else if(dateTimeData[2] >= 41 && dateTimeData[2] <= 45){ //every time related 41 second Tempeture display continiusely 5 seconds.
            getTempeture(); //display tempeture in LEDs.
            FastLED.show(); 
        }else{
            timeGetNow(); //display time in LEDs  
            FastLED.show(); 
        } 
    }

    //check time for play MP3 module stored voice
    if(dateTimeData[1] == 0 && dateTimeData[2] == 0){ //every 1 hour change voice track played relevant to it.
        execute_CMD(0x0F,1,hexaCMD[dateTimeData[0]]); //play 01 folder 001 given track
        //Serial.println("Run Voice command");
        delay(3000);
       
    }

    //mode selection
    byte btnMode = digitalRead(btnModeInput);
    if(btnMode == HIGH){  //check Mode button pressed.
        //Serial.println("Button Pressed");
        lastPressTimeBtnMode = millis(); 
        btnModVal++;   //mode button value increment till 4.(0-timeSet(),1-dateSet,2-alrmSet(),3-yearSet())
    }

    //every time check below function activities.
    timeSet();
    dateSet();
    alrmSet();
    yearSet();
    checkAlarm();  
}

/******timeGetNow()*******show time in LEDs 24 hour format.
void timeGetNow(){
    byte Hour = dateTimeData[0];    //store date/time/seconds to the veriables.
    byte Minute = dateTimeData[1];
    byte Second = dateTimeData[2];
    if(Second % 2 == 0){  //seconds inditor (2 leds) high 
        leds[42] = CRGB(0,0,0);
        leds[43] = CRGB(0,0,0);
    }else{   //seconds inditor (2 leds) low  
        leds[42] = CRGB(red,green,blue);
        leds[43] = CRGB(red,green,blue);
    }
    int nowTime = Hour * 100 + Minute;  //eg-: hour-11, minite-25 (11*100+25=1125) take Hour & Minute in a single value.
    ledDisplayGenerator(nowTime, 0, 0);  //send taken single value for generate LEDs display array. 
}*/

/******timeGetNow()********///show time in LEDs 12 hour AM/PM format.
int timeGetNow(){
    byte Hour = dateTimeData[0];    //store date/time/seconds to the veriables.
    byte Minute = dateTimeData[1];
    byte Second = dateTimeData[2];
    if(Second % 2 == 0){  //seconds inditor (2 leds) high 
        leds[42] = CRGB(0,0,0);
        leds[43] = CRGB(0,0,0);
    }else{   //seconds inditor (2 leds) low  
        leds[42] = CRGB(red,green,blue);
        leds[43] = CRGB(red,green,blue);
    }
    if(Hour > 12){
        if(Hour > 19){
            Hour = Hour % 10 + 8; 
        }else{
           Hour = Hour %10 - 2; 
        }
    }
    if(Hour == 0){
        Hour = 12;
    }
    int nowTime = Hour * 100 + Minute;  //eg-: hour-11, minite-25 (11*100+25=1125)
    ledDisplayGenerator(nowTime, 0, 0);   
}



/******dateGetNow()********///show date in LEDs.
void dateGetNow(){
    byte Month = dateTimeData[3];  //store Month & Day to the veriables.
    byte Date = dateTimeData[4];
    int monthDate = Month * 100 + Date; //eg-: month-11, date-25 (11*100+25=1125) take Month & Date in a single value.
    leds[42] = CRGB(red,green,blue); leds[43] = CRGB(red,green,blue);  //Month and Date Separete 2LEDs continuesly high
    ledDisplayGenerator(monthDate, 0, 0);
}

/******getTempeture()********///shoe tempeture in LEDs.
void getTempeture(){
     DateTime now = RTC.now(); //get realtime tempeture from RTC object
     float temp = RTC.getTemperature(); //value store in float veriable.(Eg:- 28.90) 
     int displayTemp = (temp * 100) / 10; //get tempeture in single val, Have bug when three nuber tempeture like 3.20(bug fixed 20/09/2019 through ledDisplayGenerator())
     //Serial.print(displayTemp);
     leds[42] = CRGB(0,0,0); 
     leds[43] = CRGB(red,green,blue);  //showing separetor.
     ledDisplayGenerator(displayTemp, 99, 0); //val 99 for identification purpose only."ledDisplayGenerator90" know 99 send tempeture.
}

/******timeSet()********///Set the Time
void timeSet(){
    if(btnModVal == 0){  //chk btnModVal status, 0 is Edit Time.
        editMode = true;  //since true, Time/Date/Tempeture not updating in LEDs. 
        //Serial.println("Edit Position -- 0");
        digitalWrite(ledModDate,HIGH);  //on LED relevant Set Time mode(1st LED).
        delay(400); //delay for clear button press.
        byte btnPlus = digitalRead(btnPlusInput);   //take +Plus+ button status.
        byte btnMinus = digitalRead(btnMinusInput); //take -Minus- button status.
        if(setPosition){ //if "setPosition = true" edit Hour
            setIndex = 1;  //use to setValToRTC() function direct to switch statement
            if(btnPlus == HIGH){
                increaseVal(0, 0, 1); //0 = setData[0](hour), 0 = minMaxVal[0][1](hour max val), 1 = setData[1](minute-cuple for led disply)
            }
            if(btnMinus == HIGH){
                decreaseVal(0, 0, 1); //0 = setData[0](hour), 0 = minMaxVal[0][0](hour min val), 1 = setData[1](minute-cuple for led disply)
            }
        }else{   //edit Minute
            setIndex = 2;
            if(btnPlus == HIGH){
                increaseVal(1, 1, 0); //1 = setData[1](minute), 1 = minMaxVal[1][1](minute max val), 0 = setData[0](hour-cuple for led disply)
            }
            if(btnMinus == HIGH){
                decreaseVal(1, 1, 0);
            }
        }
    } 
    setValToRTC();  //write updated values to RTC.
    reset();  //reset edit mode status.
}

/******dateSet()********///Set the Date
void dateSet(){
    if(btnModVal == 1){  //chk btnModVal status, 1 is Edit Date.
        editMode = true;
        //Serial.println("Edit Position -- 1");
        digitalWrite(ledModTime,HIGH); //on LED relevant Set Date mode(2nd LED).
        delay(400);
        byte btnPlus = digitalRead(btnPlusInput);   
        byte btnMinus = digitalRead(btnMinusInput); 
        if(setPosition){ //if "setPosition = true" edit Month
            setIndex = 3;  //use to setValToRTC() function direct to switch statement  
            if(btnPlus == HIGH){
                increaseVal(3, 2, 4);  //3 = setData[3](month), 2 = minMaxVal[2][1](month max val), 4 = setData[4](date-cuple for led disply)
            }
            if(btnMinus == HIGH){
                decreaseVal(3, 2, 4);
            }
        }else{  //edit Date
            setIndex = 4;
            if(btnPlus == HIGH){
                increaseVal(4, 3, 3);//3
            }
            if(btnMinus == HIGH){
                decreaseVal(4, 3, 3); //4 = setData[4](day), 3 = minMaxVal[1][1](minute min val), 3 = setData[3](month-cuple for led disply)
            }
        }
    } 
    setValToRTC();
    reset();
}

/******alrmSet()********///Setting Alrm
void alrmSet(){
    if(btnModVal == 2){ //chk btnModVal status, 2 is Set alarm.
        editMode = true;
        //Serial.println("Edit Position -- 2");
        digitalWrite(ledModAlarm,HIGH); 
        delay(400);
        byte btnPlus = digitalRead(btnPlusInput);   
        byte btnMinus = digitalRead(btnMinusInput); 
        if(setPosition){ //if "setPosition = true" edit elarm Hour
            setIndex = 5; //this go to setValToRTC()but not write to RTC, just store valu in setData[].
            if(btnPlus == HIGH){
                increaseVal(6, 0, 7); 
            } 
            if(btnMinus == HIGH){
                decreaseVal(6, 0, 7);
            }
        }else{ //edit Minute
            setIndex = 6;
            if(btnPlus == HIGH){
                increaseVal(7, 1, 6);
            }
            if(btnMinus == HIGH){
                decreaseVal(7, 1, 6);
            }  
        }
    }
    setValToRTC(); 
    reset();
}

/******yearSet()********///srtting year
void yearSet(){
    if(btnModVal == 3){
        editMode = true;
        setIndex = 7;
        digitalWrite(ledModDate,HIGH);
        digitalWrite(ledModTime,HIGH);
        digitalWrite(ledModAlarm,HIGH);
        delay(400);
        //Serial.println("------Year Edit Mode------");
        byte btnPlus = digitalRead(btnPlusInput);   
        byte btnMinus = digitalRead(btnMinusInput); 
        if(btnPlus == HIGH){
            increaseVal(5, 4, 0);
        }
        if(btnMinus == HIGH){
            decreaseVal(5,4, 0);
        }
    }
    setValToRTC();
    reset();
}

/******checkAlarm()********///Check Alrm is On & exit edit mode RESET
void checkAlarm(){
    byte btnElarmStop = digitalRead(btnAlrmOffInput);
    if(((dateTimeData[0] == setData[6]) && (dateTimeData[1] == setData[7]) && alarmSet) || alarmBeepUntillStop){
        //Serial.print(dateTimeData[0]); Serial.print("==");  Serial.print(setData[6]); Serial.print("------"); Serial.print(dateTimeData[1]); Serial.print("==");  Serial.print(setData[7]);
        //Serial.print("--------alarmBeepUntillStop=====");  Serial.print(alarmBeepUntillStop);
        Serial.println("Alrm beeeeeeeeeeeeeeeeeep");
        alarmBeepUntillStop = true;
        if(!alarmPlayExecute){
            alarmPlayExecute = true; //value true for stop iterate play values to mp3 module
            execute_CMD(0x17,0,2); //loop play folder 002 content
            delay(100);
        }
    }
    if(btnElarmStop == HIGH && editMode){ //reset from edit mode.exit edit mode.
        btnModVal = 4; //4 is reset value.check reset().
    }
    if(btnElarmStop == HIGH){ //chk elarmStopBtn is pressed
        alarmBeepUntillStop = false;
        alarmSet = false;
        alarmPlayExecute = false; //stop iterate alarm loopingcommand execute to mp module
        execute_CMD(0x16,0,0); //stop playback
        delay(100);
        setData[6] = -1;  //reset alrm set values in setData[] array.
        setData[7] = -1;
    }
}

/******reset()********///reset mode LED and some veriable values
void reset(){
    digitalWrite(ledModDate,LOW);  //Off each mode leds.
    digitalWrite(ledModTime,LOW);
    digitalWrite(ledModAlarm,LOW);
    if(btnModVal == 4 || millis() - lastPressTimeBtnMode >= 300000){  //if not reset, after 5 minute it will be reset. 4 is last mode value.it use as reset value.
        digitalWrite(ledModDate,LOW);
        digitalWrite(ledModTime,LOW);
        digitalWrite(ledModAlarm,LOW); 
        btnModVal = -1; //reset btnModVal value.
        setPosition = true; //reset setPosition value.
        editMode = false;
    }
}

/******ledDisplayGenerator()********/
void ledDisplayGenerator(int Now, byte firstCuple, byte secndCuple){
    int nowVal = Now;
    for(byte i = 0; i < 4; i++){  //4-four digits (two for hour/month & two for minute/date).
        if(Now == 0 && i == 0){  //if Now parameter empty led shows edit mode minute/date (3 and 4 digit)
            nowVal = secndCuple;
        }
        if(Now == 0 && i == 2){  //if Now parameter empty led shows edit mode Hour/month (1 and 2 digit)
            nowVal = firstCuple;
        }
        byte digit = nowVal % 10;   //only filter each last digits in queue (Eg: 1245 - take 5)
        //Serial.print("Digit Value--");
        //Serial.println(digit);
        if(i == 0){  //4th digit lightup.
            if(firstCuple == 99){ //99 for identyfy purpose only. when I passed tempeture to "Now" parameter I sent "firstCuple" parameter value as 99
                digit = 10; //since "C" letter represent in digits[11][21] array 10th index.
            }
            byte digitStart = 65;  //4th digit starting point
            //Serial.print("__Digit 4--");
            for(byte k = 0; k < 21; k++){  //k is one digit include nos LEDs in one seven segment.(21=3*7)
                //Serial.print(digits[digit][k]);    
                if(digits[digit][k] == 1){  //
                    leds[digitStart] = CRGB(red,green,blue); //color of LED lighted
                }else{
                    leds[digitStart] = CRGB(0,0,0);  //off colored LED(black)
                }
                digitStart++; 
            } //Serial.println();
        }else if(i == 1){  //3rd digit lightup
            byte digitStart = 44;  //3rd digit starting point
            //Serial.print("__Digit 3--");
            for(byte k = 0; k < 21; k++){  
                //Serial.print(digits[digit][k]);      
                if(digits[digit][k] == 1){
                    leds[digitStart] = CRGB(red,green,blue);
                }else{
                    leds[digitStart] = CRGB(0,0,0);
                }
                digitStart++; 
            }  //Serial.println();
        }else if(i == 2){  //2nd digit lightup
            byte digitStart = 21;  //2nd digit starting point
            //Serial.print("__Digit 2--"); 
            for(byte k = 0; k < 21; k++){ 
                //Serial.print(digits[digit][k]);      
                if(digits[digit][k] == 1){
                    leds[digitStart] = CRGB(red,green,blue);
                }else{
                    leds[digitStart] = CRGB(0,0,0);
                }
                digitStart++; 
            } //Serial.println();
        }else if(i == 3){  //1st digit lightup
            byte digitStart = 0;  //1st digit starting point
            //Serial.print("__Digit 1--");
            for(byte k = 0; k < 21; k++){ 
                //Serial.print(digits[digit][k]);      
                if(digits[digit][k] == 0 || (digit == 0 && dateTimeData[0] != 0)){ //if 1st digit 0 it belongs all LEDs off (leading zero not showing)
                    leds[digitStart] = CRGB(0,0,0);                                      //but midnight 24 hour showing as 00
                    //Serial.print("OFF"); 
                }else{
                    leds[digitStart] = CRGB(red,green,blue); 
                }
                digitStart++;  
            } //Serial.println();
        }
        nowVal = (firstCuple == 99 && i == 0) ? Now:  nowVal/10; //4digit not taken value from tempeture.it showing "C" letter. thats why this filter nextval for 4th digit.
        //Serial.print("Next Now----");   Serial.print(nowVal);
        //Serial.println();
    }
}

/******setValToRTC()********///Edit functions values write to RTC.
void setValToRTC(){
    byte btnSet = digitalRead(btnSetInput); //check SET button is pressed.
    if(btnSet == HIGH){
        //Serial.println("Set Button Pressed");
        switch(setIndex){ //check what is the "setIndex" value.
            case 1:  //hour set
                setPosition = false; //allow next element (minute) to edit.
                writeToRTC(3, 0);  //send data to writeToRTC() function. 3(rtcQueue[3]-located inside writeToRTC function), 0(setData[0]-array)
                delay(1500);
            break;
            case 2:  //minute set
                setPosition = true;  //set to default value (Hour) edit.
                btnModVal = 4;  //for reset btnModVal and LED off according to it.see reset() function. 
                setIndex = 0;  //back to default value.swich statement need thisvalue.
                writeToRTC(4, 1);
                editMode = false;
                delay(1500);
            break;
            case 3:  //month set
                setPosition = false; //allow next element (minute) to edit.
                writeToRTC(1, 3);  
                delay(1500);
            break;
            case 4:  //date set
                setPosition = true;  //set todefault value (Hour) edit.
                btnModVal = 4;  //for reset btnModVal and LED off according to it.see reset() function. 
                setIndex = 0;  
                writeToRTC(2, 4);
                delay(1500);
                editMode = false;
            break;
            case 5: //alrm hour set
                setPosition = false; //allow next element (minute) to edit.
                //alarmSet = true; //alrm set value become true
                delay(2500);
            break;
            case 6:  //alarm minute set
                setPosition = true;  //set to default value (Hour) edit.
                alarmSet = true; //alrm set value become true
                btnModVal = 4;  //for reset btnModVal and LED off according to it.see reset() function. 
                setIndex = 0;  //back to default value.swich statement need thisvalue.
                delay(2500);
                editMode = false;
            break;
            case 7:  //Year set
                btnModVal = 4;  //for reset btnModVal and LED off according to it.see reset() function. 
                setIndex = 0;  //back to default value.swich statement need thisvalue.
                writeToRTC(0, 5);
                delay(2500);
                editMode = false;
            break;
            default:
                //Serial.println("ignor");
                editMode = false;
            break;
        }
    }
}

/******writeToRTC()********///send updated values to RTC
void writeToRTC(byte writeIndex, byte setDataIndex){  //writeIndex for rtcQueue[], setDataIndex for setData[].
    int rtcQueue[] = {dateTimeData[5], dateTimeData[3], dateTimeData[4], dateTimeData[0], dateTimeData[1]};//YYYY[0],MM[1],DD[2],HH[3],MIN[4]
    rtcQueue[writeIndex] = setData[setDataIndex]; //write updated value to the rtcQueue[] from setData[] array.
    dateTimeData[setDataIndex] = setData[setDataIndex];
    /*Serial.print("rtcQueue[i]----");
    for(byte i=0; i<5;i++){
      Serial.print(rtcQueue[i]);
      Serial.print("["); Serial.print(i);  Serial.print("]");
    } Serial.println();
    Serial.print("setData[i]----");
    for(byte i=0; i<8;i++){
      Serial.print(setData[i]);
      Serial.print("["); Serial.print(i);  Serial.print("]");
    }Serial.println();
    Serial.print("dateTimeData[i]----");
    for(byte i=0; i<6;i++){
      Serial.print(dateTimeData[i]);
      Serial.print("["); Serial.print(i);  Serial.print("]");
    }Serial.println();*/
    RTC.adjust(DateTime(rtcQueue[0], rtcQueue[1], rtcQueue[2], rtcQueue[3], rtcQueue[4], 0)); //YYYY[0],MM[1],DD[2],HH[3],MIN[4],Sec[5]
}

/******increaseVal()*******/
void increaseVal(byte setDataArrayPos, byte arrayIndex, byte cupleValIndex){  //setDataArrayPos(location of"setData[]"),arrayIndex(relevant max value of index"minMaxVal[5][2]" & its position "arrayPos")
    setData[setDataArrayPos] = setData[setDataArrayPos] + 1; //increase value according to btnPlus pressed.
    setData[setDataArrayPos] = (setData[setDataArrayPos] < minMaxVal[arrayIndex][1]) ? setData[setDataArrayPos] : minMaxVal[arrayIndex][0]; //chk value greater than max value and store to setData array.
    //Serial.println(setData[setDataArrayPos]);
    if(setPosition){
        if(setDataArrayPos == 5){ //this is for year increase only,Since year has 4numbers. it fitted to ledDisplayGenerator() perfectly:)
            ledDisplayGenerator(setData[setDataArrayPos], 0, 0);
            FastLED.show();  
            //Serial.print("----------------------------------");
            //Serial.println(setData[setDataArrayPos]);
        }else{
            byte minusValChk = (setData[cupleValIndex] == -1) ? 0 : setData[cupleValIndex];
            leds[42] = CRGB(red,green,blue); leds[43] = CRGB(red,green,blue);
            ledDisplayGenerator(0, setData[setDataArrayPos], minusValChk); //0 send as 1st parameter since this is not date/time value. 2nd parameter represent 4th and 3rd digit, 3rd parameter represent 2nd and 1st digit 
            FastLED.show(); 
            //Serial.print("----------------------------------");
            //Serial.print(setData[setDataArrayPos]);  //Serial.println(minusValChk);
        }
    }else{
        byte minusValChk = (setData[cupleValIndex] == -1) ? 0 : setData[cupleValIndex];
        leds[42] = CRGB(red,green,blue); leds[43] = CRGB(red,green,blue);
        ledDisplayGenerator(0, minusValChk, setData[setDataArrayPos]);
        FastLED.show(); 
        //Serial.print("----------------------------------");
        //Serial.print(minusValChk);  //Serial.println(setData[setDataArrayPos]); 
    }
    delay(40);  
}

/******decreaseVal()*******/
void decreaseVal(byte setDataArrayPos, byte arrayIndex, byte cupleValIndex){
    setData[setDataArrayPos] = (setData[setDataArrayPos] <= minMaxVal[arrayIndex][0]) ?  minMaxVal[arrayIndex][1] : setData[setDataArrayPos]; //chk value less than min value and store to setData array.
    setData[setDataArrayPos] = setData[setDataArrayPos] - 1; //decrease value according to btnMinus pressed.
    //Serial.println(setData[setDataArrayPos]);
    if(setPosition){
        if(setDataArrayPos == 5){ //this is for year decrease only
            ledDisplayGenerator(setData[setDataArrayPos], 0, 0);
            FastLED.show();  
            //Serial.print("----------------------------------");
            //Serial.println(setData[setDataArrayPos]);
        }else{
            byte minusValChk = (setData[cupleValIndex] == -1) ? 0 : setData[cupleValIndex];
            leds[42] = CRGB(red,green,blue); leds[43] = CRGB(red,green,blue); //hour/month and minute/date separetor allways high in edit mode
            ledDisplayGenerator(0, setData[setDataArrayPos], minusValChk);
            FastLED.show(); 
            //Serial.print("----------------------------------");
            //Serial.print(setData[setDataArrayPos]);  //Serial.println(minusValChk);
        }
    }else{
        byte minusValChk = (setData[cupleValIndex] == -1) ? 0 : setData[cupleValIndex];
        leds[42] = CRGB(red,green,blue); leds[43] = CRGB(red,green,blue);
        ledDisplayGenerator(0, minusValChk, setData[setDataArrayPos]);
        FastLED.show(); 
        //Serial.print("----------------------------------");
        //Serial.print(minusValChk);  //Serial.println(setData[setDataArrayPos]);
    }
    delay(40);
}

/******MP3 module command executer*******/
/*
General DF Player mini command structure (only byte 3, 5 and 6 to be entered in the serial monitor):
~~~~~~~~~~~~~~~~~~~~~~~~~~~~~~~~~~~~~~~~~~~~~~~~~~~~~~~~~~~~~~~~~~~~~~~~~~~~~~~~~~~~~~~~~~~~~~~~~~~~
Byte Function Value
==== ================ ====
(0) Start Byte 0x7E
(1) Version Info 0xFF (don't know why it's called Version Info)
(2) Number of bytes 0x06 (Always 6 bytes)
(3) Command 0x__
(4) Command feedback 0x__ If enabled returns info with command 0x41 [0x01: info, 0x00: no info]
(5) Parameter 1 [DH] 0x__
(6) Parameter 2 [DL] 0x__
(7) Checksum high 0x__ See explanation below. Is calculated in function: execute_CMD
(8) Checksum low 0x__ See explanation below. Is calculated in function: execute_CMD
(9) End command 0xEF

Checksum calculation.
~~~~~~~~~~~~~~~~~~~~
Checksum = -Sum(byte(1..6)) (2 bytes, notice minus sign!)
*/
void execute_CMD(byte CMD, byte Par1, byte Par2){
    // Calculate the checksum (2 bytes)
    word checksum = -(Version_Byte + Command_Length + CMD + Acknowledge + Par1 + Par2);
    // Build the command line
    byte Command_line[10] = { 
                                Start_Byte, 
                                Version_Byte, 
                                Command_Length, 
                                CMD, 
                                Acknowledge,
                                Par1, 
                                Par2, 
                                highByte(checksum), 
                                lowByte(checksum), 
                                End_Byte
                             };
    //Send the command line to the module
    for (byte k=0; k<10; k++){
        mySerial.write( Command_line[k]);
    }
}
